# Fritzing sketch Home_Automation_Sensor_Monitoring (saved by Fritzing 0.9.3b)

parts:
  U3 = ESP8266 NodeMCU LoLin module
  LED7 = LED - 5mm [color="Red (633nm)" package="5 mm [THT]"]
  LED8 = LED - 5mm [color="Red (633nm)" package="5 mm [THT]"]
  LED9 = LED - 5mm [color="Red (633nm)" package="5 mm [THT]"]
  e-radionica_com3 = LM393 LDR breakout [part_number=100027]

nets:
  N1: U3.D1, LED7.anode
  N2: U3.D2, LED8.anode
  N3: U3.D3, LED9.anode
  GND: U3.GND, LED7.cathode, e-radionica_com3.GND
  3V3: U3.3V3, e-radionica_com3.VCC, e-radionica_com3.DO
  N4: U3.A0, e-radionica_com3.AO

custom parts:
  ESP8266 NodeMCU LoLin module: ESP8266 based NodeMCU
